// Logisim project sample13.tex.circ as structural Verilog
module main (
  input  in_1,
  input  in_2
);

  wire and_1_out, and_2_out, and_3_out, and_4_out, not_1_out, not_2_out;

  not not_1 (not_1_out, in_1);
  not not_2 (not_2_out, in_1);
  and and_1 (and_1_out, in_2, not_2_out, not_1_out);
  and and_2 (and_2_out, in_2, in_2, in_1, not_1_out);
  and and_3 (and_3_out, not_2_out, in_1, in_2);
  and and_4 (and_4_out, in_1, in_1, in_2, in_2);
  // Pins of 1 and 2 bits meet at {2{in_1}}
endmodule

module sample2 (
  input  in_1
);

  wire and_1_out, and_2_out, and_3_out, and_4_out, not_1_out, not_2_out;
  wire [1:1] undriven;

  not not_1 (not_1_out, undriven[1]);
  not not_2 (not_2_out, in_1);
  and and_1 (and_1_out, not_2_out, not_1_out);
  and and_2 (and_2_out, in_1, not_1_out);
  and and_3 (and_3_out, not_2_out, undriven[1]);
  and and_4 (and_4_out, in_1, undriven[1]);
  // Pins of 1 and 2 bits meet at {undriven[1], in_1}
endmodule

module sample3 (
  input  in_1,
  input  in_2,
  input  in_3,
  input  in_4
);

  wire and_1_out, not_1_out, or_1_out, or_2_out;

  not not_1 (not_1_out, in_2);
  and and_1 (and_1_out, in_3, not_1_out);
  or or_1 (or_1_out, and_1_out, in_1);
  or or_2 (or_2_out, in_2, in_1);
endmodule

module sample4 (
  input  in_1
);

  wire nand_1_out;

  nand nand_1 (nand_1_out, in_1, in_1);
  // Probe on nand_1_out
endmodule

module sample5 (
  input  [1:0] in_1
);

  wire nand_1_out, nand_2_out;

  nand nand_1 (nand_1_out, in_1[0], in_1[1]);
  nand nand_2 (nand_2_out, nand_1_out, nand_1_out);
  // Probe on nand_2_out
endmodule

module sample6 (
  input  in_1,
  input  in_2
);

  wire nand_1_out, nand_2_out, nand_3_out;

  nand nand_1 (nand_1_out, in_1, in_1);
  nand nand_2 (nand_2_out, in_2, in_2);
  nand nand_3 (nand_3_out, nand_1_out, nand_2_out);
  // Probe on nand_3_out
endmodule

module smaple7 (
  input  in_1,
  input  in_2
);

  wire nand_1_out, nand_2_out, nand_3_out, nand_4_out;

  nand nand_1 (nand_1_out, in_1, in_1);
  nand nand_2 (nand_2_out, in_2, in_2);
  nand nand_3 (nand_3_out, nand_1_out, nand_2_out);
  nand nand_4 (nand_4_out, nand_3_out, nand_3_out);
  // Probe on nand_4_out
endmodule

module sample8 (
  input  in_1,
  input  in_2
);

  wire nand_1_out, nand_2_out, nand_3_out, nand_4_out;

  nand nand_1 (nand_1_out, in_1, in_2);
  nand nand_2 (nand_2_out, in_1, nand_1_out);
  nand nand_3 (nand_3_out, nand_1_out, in_2);
  nand nand_4 (nand_4_out, nand_2_out, nand_3_out);
  // Probe on nand_4_out
endmodule

module sample9 (
  input  in_1
);

  wire nor_1_out;

  nor nor_1 (nor_1_out, in_1, in_1);
  // Probe on nor_1_out
endmodule

module sample10 (
  input  in_1,
  input  in_2
);

  wire nor_1_out, nor_2_out, nor_3_out;

  nor nor_1 (nor_1_out, in_1, in_1);
  nor nor_2 (nor_2_out, in_2, in_2);
  nor nor_3 (nor_3_out, nor_1_out, nor_2_out);
  // Probe on nor_3_out
endmodule

module sample11 (
  input  [1:0] in_1
);

  wire nor_1_out, nor_2_out;

  nor nor_1 (nor_1_out, in_1[0], in_1[1]);
  nor nor_2 (nor_2_out, nor_1_out, nor_1_out);
  // Probe on nor_2_out
endmodule

module sample12 (
  input  in_1,
  input  in_2
);

  wire nor_1_out, nor_2_out, nor_3_out, nor_4_out;

  nor nor_1 (nor_1_out, in_1, in_1);
  nor nor_2 (nor_2_out, in_2, in_2);
  nor nor_3 (nor_3_out, nor_1_out, nor_2_out);
  nor nor_4 (nor_4_out, nor_3_out, nor_3_out);
  // Probe on nor_4_out
endmodule

module sample13 (
  input  in_1,
  input  in_2
);

  wire nor_1_out, nor_2_out, nor_3_out, nor_4_out, nor_5_out;

  nor nor_1 (nor_1_out, in_1, in_2);
  nor nor_2 (nor_2_out, in_1, nor_1_out);
  nor nor_3 (nor_3_out, nor_1_out, in_2);
  nor nor_4 (nor_4_out, nor_2_out, nor_3_out);
  // Probe on nor_5_out
  nor nor_5 (nor_5_out, nor_4_out, nor_4_out);
endmodule

module sample14 (
  input  in_1
);

  wire nand_1_out, nand_2_out, nand_3_out;

  nand nand_1 (nand_1_out, in_1, in_1);
  nand nand_2 (nand_2_out, in_1, nand_1_out);
  nand nand_3 (nand_3_out, nand_2_out, nand_2_out);
  // Probe on nand_3_out
endmodule

module sample15 (
  input  in_1
);

  wire nand_1_out, nand_2_out, nand_3_out, nand_4_out;

  nand nand_1 (nand_1_out, in_1, in_1);
  nand nand_2 (nand_2_out, in_1, in_1);
  nand nand_3 (nand_3_out, nand_1_out, nand_1_out);
  nand nand_4 (nand_4_out, nand_2_out, nand_3_out);
  // Probe on nand_4_out
endmodule

module sample16 (
  input  in_1
);

  wire nor_1_out, nor_2_out, nor_3_out;

  nor nor_1 (nor_1_out, in_1, in_1);
  nor nor_2 (nor_2_out, in_1, nor_1_out);
  nor nor_3 (nor_3_out, nor_2_out, nor_2_out);
  // Probe on nor_3_out
endmodule

module sample17 (
  input  in_1
);

  wire nor_1_out, nor_2_out, nor_3_out, nor_4_out;

  nor nor_1 (nor_1_out, in_1, in_1);
  nor nor_2 (nor_2_out, in_1, in_1);
  nor nor_3 (nor_3_out, nor_1_out, nor_1_out);
  nor nor_4 (nor_4_out, nor_2_out, nor_3_out);
  // Probe on nor_4_out
endmodule
